# Fritzing sketch Schema 1 - Sending Text (saved by Fritzing 0.9.3b)

parts:
  Part1 = Arduino Nano (Rev3.0) (ICSP)
  Part3 = NRF24L01+ Breakout Board
  C1 = Electrolytic Capacitor [capacitance=100μF package="0807 [SMD, electrolytic]"]  # not connected
  Part4 = Arduino Nano (Rev3.0) (ICSP)
  Part5 = NRF24L01+ Breakout Board
  C2 = Electrolytic Capacitor [capacitance=100μF package="0807 [SMD, electrolytic]"]  # not connected

nets:
  N1: Part1.D8, Part3.CS
  N2: Part1.D9, Part3.CE
  N3: Part1.D11/MOSI, Part3.MOSI
  N4: Part1.D12/MISO, Part3.MISO
  GND: Part1.GND, Part3.GND
  3V3: Part1.3V3, Part3.VCC
  N5: Part1.D13/SCK, Part3.SCK
  N6: Part4.D8, Part5.CS
  N7: Part4.D9, Part5.CE
  N8: Part4.D11/MOSI, Part5.MOSI
  N9: Part4.D12/MISO, Part5.MISO
  GND_2: Part4.GND, Part5.GND
  3V3_2: Part4.3V3, Part5.VCC
  N10: Part4.D13/SCK, Part5.SCK
