# Fritzing sketch Schema 2 - Lighting Up LEDs (saved by Fritzing 0.9.3b)

parts:
  Part1 = Arduino Nano (Rev3.0) (ICSP)
  Part3 = NRF24L01+ Breakout Board
  C1 = Electrolytic Capacitor [capacitance=100μF package="0807 [SMD, electrolytic]"]  # not connected
  Part4 = Arduino Nano (Rev3.0) (ICSP)
  Part5 = NRF24L01+ Breakout Board
  C2 = Electrolytic Capacitor [capacitance=100μF package="0807 [SMD, electrolytic]"]  # not connected
  S1 = Pushbutton [package="[THT]"]
  S2 = Pushbutton [package="[THT]"]
  R1 = Resistor [tolerance=±5% resistance=100 package=THT]
  R2 = Resistor [tolerance=±5% resistance=100 package=THT]
  LED1 = LED - 5mm [color="Red (633nm)" package="5 mm [THT]"]
  LED2 = LED - 5mm [color="Blue (525nm)" package="5 mm [THT]"]
  R3 = Resistor [tolerance=±5% resistance=220 package=THT]

nets:
  GND: Part1.GND, Part3.GND, R1.Pin_0, R2.Pin_0
  N1: Part1.D3, S2.Pin_1
  N2: Part1.D4, S1.Pin_1, S1.Pin_2
  N3: Part1.D8, Part3.CS
  N4: Part1.D9, Part3.CE
  N5: Part1.D11/MOSI, Part3.MOSI
  N6: Part1.D12/MISO, Part3.MISO
  N7: Part1.5V, S2.Pin_3, S2.Pin_4
  3V3: Part1.3V3, Part3.VCC
  N8: Part1.D13/SCK, Part3.SCK
  GND_2: Part4.GND, Part5.GND, R3.Pin_0
  N9: Part4.D5, LED2.anode
  N10: Part4.D6, LED1.anode
  N11: Part4.D8, Part5.CS
  N12: Part4.D9, Part5.CE
  N13: Part4.D11/MOSI, Part5.MOSI
  N14: Part4.D12/MISO, Part5.MISO
  3V3_2: Part4.3V3, Part5.VCC
  N15: Part4.D13/SCK, Part5.SCK
  N16: LED1.cathode, LED2.cathode, R3.Pin_1
